# Fritzing sketch Main_Demo (saved by Fritzing 1.0.6)
breadboards: 1

parts:
  MBED1 = mbed
  DRV8832 = DRV8832 [package=10-pin]
  LD33 = V_REG_LD1117VXX [package=78xxl]
  M1 = DC Motor [voltage_(max)=6V voltage_(min)=3V]
  R1 = Resistor [tolerance=±5% resistance=100 package="0805 [SMD]"]
  LED1 = LED - 5mm [color="Red (633nm)" current=0.030A package="5 mm [THT]"]
  C1 = Electrolytic Capacitor [capacitance=47µF voltage=35V package="100 mil [THT, electrolytic]"]
  C2 = Ceramic Capacitor [capacitance=100nF voltage=35V package="100 mil [THT, multilayer]"]
  C3 = Ceramic Capacitor [capacitance=100nF voltage=35V package="100 mil [THT, multilayer]"]
  VCC1 = 4 x AAA Battery Mount [internal_resistance=0.1Ω]
  C4 = Ceramic Capacitor [capacitance=100nF voltage=35V package="100 mil [THT, multilayer]"]
  Q1 = TPR-105F [package=qrb1114-side]  # not connected
  R2 = Resistor [tolerance=±5% power=0.25W resistance=10k package=THT]  # not connected
  Q2 = TPR-105F [package=qrb1114-side]  # not connected

nets:
  GND: MBED1.GND, DRV8832.ISENSE, DRV8832.GND, LD33.GND, LED1.cathode, C1.-, C2.0, C3.0, VCC1.-, C4.0
  VIN: MBED1.Vin, DRV8832.VCC, LD33.IN, C2.1, C3.1, VCC1.+, C4.1
  N1: MBED1.pin13, DRV8832.IN2
  N2: MBED1.pin14, DRV8832.IN1
  N3: MBED1.pin18, DRV8832.VSET
  N4: DRV8832.OUT2, M1.pin_1
  N5: DRV8832.OUT1, M1.pin_2
  N6: LD33.OUT, R1.Pin_1, C1.+
  N7: R1.Pin_0, LED1.anode

custom parts:
  mbed: A powerful microcontroller board based on the NXP LPC processor with an ARM Cortex core. See http://mbed.org for more info.
  TPR-105F: PHOTOTRANSISTOR REFLECTIVE OBJECT SENSOR The QRB1113/1114 consists of an infrared emitting diode and an NPN silicon phototransistor mounted side by side on a converging optical axis in a black plastic housing. The phototransistor responds to radiation from the emitting diode only when a reflective object passes within its field of view. The area of the optimum response approximates a circle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
